# Fritzing sketch arduino_temperature_and_display (saved by Fritzing 0.8.7b)
breadboards: 1

parts:
  Part1 = Arduino Uno (Rev3) - ICSP
  U1 = TMP36 [package=to-92]
  4Digit_7SEG1 = Sparkfun 4-digit 7-segment LED Display

nets:
  N1: Part1.A0, U1.VOUT
  N2: Part1.D10_PWM/SS, 4Digit_7SEG1.CSN
  N3: Part1.D11_PWM/MOSI, 4Digit_7SEG1.SI
  N4: Part1.D13/SCK, 4Digit_7SEG1.SCK
  VCC: Part1.AREF, Part1.3V3, U1.VCC, 4Digit_7SEG1.VCC
  GND: Part1.GND, U1.GND, 4Digit_7SEG1.GND

custom parts:
  Sparkfun 4-digit 7-segment LED Display: 4-digit, 7-segment LED Display with SPI/Serial Control
